// Logisim project OAC.circ as structural Verilog: 1 circuit, main circuit main
module main (
  input  in_1,
  output out_2,
  output out_3,
  output out_4,
  output out_5,
  output out_6
);

  wire and_1_out, and_2_out, and_3_out;

  J_K_Flip_Flop j_k_ff_1 (.J(1'b1), .clk(in_1), .K(1'b1), .Q(out_2));  // open: Qn, preset, en, reset
  J_K_Flip_Flop j_k_ff_2 (.J(out_2), .clk(in_1), .K(out_2), .Q(out_3));  // open: Qn, preset, en, reset
  and and_1 (and_1_out, out_2, out_3);
  J_K_Flip_Flop j_k_ff_3 (.J(and_1_out), .clk(in_1), .K(and_1_out), .Q(out_4));  // open: Qn, preset, en, reset
  and and_2 (and_2_out, and_1_out, out_4);
  J_K_Flip_Flop j_k_ff_4 (.J(and_2_out), .clk(in_1), .K(and_2_out), .Q(out_5));  // open: Qn, preset, en, reset
  and and_3 (and_3_out, and_2_out, out_5);
  J_K_Flip_Flop j_k_ff_5 (.J(and_3_out), .clk(in_1), .K(and_3_out), .Q(out_6));  // open: Qn, preset, en, reset
endmodule
