// Logisim project Relogio.circ as structural Verilog: 5 circuits, main circuit main
module Contador0_9 (
  input  Reset,
  input  Clock,
  output B,
  output A,
  output D,
  output C
);

  wire and_1_out, and_2_out, and_3_out, and_4_out, or_1_out;

  J_K_Flip_Flop j_k_ff_1 (.J(1'b1), .clk(Clock), .K(1'b1), .Q(D), .reset(or_1_out));  // open: Qn, preset, en
  and and_1 (and_1_out, C, A);
  J_K_Flip_Flop j_k_ff_2 (.J(D), .clk(Clock), .K(D), .Q(C), .reset(or_1_out));  // open: Qn, preset, en
  and and_2 (and_2_out, D, C);
  and and_3 (and_3_out, and_2_out, B);
  J_K_Flip_Flop j_k_ff_3 (.J(and_2_out), .clk(Clock), .K(and_2_out), .Q(B), .reset(or_1_out));  // open: Qn, preset, en
  J_K_Flip_Flop j_k_ff_4 (.J(and_3_out), .clk(Clock), .K(and_3_out), .Q(A), .reset(or_1_out));  // open: Qn, preset, en
  and and_4 (and_4_out, B, A);
  or or_1 (or_1_out, and_4_out, and_1_out, Reset);
endmodule

module main (
);

  wire clock_1_out, contador0_2_1_a, contador0_2_1_b, contador0_5_1_a, contador0_5_1_b, contador0_5_1_c,
       contador0_5_2_a, contador0_5_2_b, contador0_5_2_c, contador0_9_1_a, contador0_9_1_b, contador0_9_1_c,
       contador0_9_1_d, contador0_9_2_a, contador0_9_2_b, contador0_9_2_c, contador0_9_2_d, contador0_9_3_a,
       contador0_9_3_b, contador0_9_3_c, contador0_9_3_d, decodificar_7_seguimentos_1_a_2,
       decodificar_7_seguimentos_1_b_2, decodificar_7_seguimentos_1_c_2, decodificar_7_seguimentos_1_d_2,
       decodificar_7_seguimentos_1_e, decodificar_7_seguimentos_1_f, decodificar_7_seguimentos_1_g,
       decodificar_7_seguimentos_2_a_2, decodificar_7_seguimentos_2_b_2, decodificar_7_seguimentos_2_c_2,
       decodificar_7_seguimentos_2_d_2, decodificar_7_seguimentos_2_e, decodificar_7_seguimentos_2_f,
       decodificar_7_seguimentos_2_g, decodificar_7_seguimentos_3_a_2, decodificar_7_seguimentos_3_b_2,
       decodificar_7_seguimentos_3_c_2, decodificar_7_seguimentos_3_d_2, decodificar_7_seguimentos_3_e,
       decodificar_7_seguimentos_3_f, decodificar_7_seguimentos_3_g, decodificar_7_seguimentos_4_a_2,
       decodificar_7_seguimentos_4_b_2, decodificar_7_seguimentos_4_c_2, decodificar_7_seguimentos_4_d_2,
       decodificar_7_seguimentos_4_e, decodificar_7_seguimentos_4_f, decodificar_7_seguimentos_4_g,
       decodificar_7_seguimentos_5_a_2, decodificar_7_seguimentos_5_b_2, decodificar_7_seguimentos_5_c_2,
       decodificar_7_seguimentos_5_d_2, decodificar_7_seguimentos_5_e, decodificar_7_seguimentos_5_f,
       decodificar_7_seguimentos_5_g, decodificar_7_seguimentos_6_a_2, decodificar_7_seguimentos_6_b_2,
       decodificar_7_seguimentos_6_c_2, decodificar_7_seguimentos_6_d_2, decodificar_7_seguimentos_6_e,
       decodificar_7_seguimentos_6_f, decodificar_7_seguimentos_6_g, nor_1_out, nor_2_out, nor_3_out,
       nor_4_out, nor_5_out;

  nor nor_1 (nor_1_out, contador0_9_1_d, contador0_9_1_c, contador0_9_1_b, contador0_9_1_a);
  Clock clock_1 (.out(clock_1_out));
  Contador0_9 contador0_9_1 (
    .C(contador0_9_1_c), .B(contador0_9_1_b), .A(contador0_9_1_a), .Clock(clock_1_out), .D(contador0_9_1_d));  // open: Reset
  Contador0_2 contador0_2_1 (.Clock(nor_3_out), .B(contador0_2_1_b), .A(contador0_2_1_a));  // open: Reset
  Contador0_5 contador0_5_1 (
    .Clock(nor_1_out), .C(contador0_5_1_c), .A(contador0_5_1_a), .B(contador0_5_1_b));  // open: Reset
  Contador0_9 contador0_9_2 (
    .C(contador0_9_2_c), .B(contador0_9_2_b), .A(contador0_9_2_a), .Clock(nor_4_out), .D(contador0_9_2_d));  // open: Reset
  Contador0_5 contador0_5_2 (
    .Clock(nor_5_out), .C(contador0_5_2_c), .A(contador0_5_2_a), .B(contador0_5_2_b));  // open: Reset
  Contador0_9 contador0_9_3 (
    .C(contador0_9_3_c), .B(contador0_9_3_b), .A(contador0_9_3_a), .Clock(nor_2_out), .D(contador0_9_3_d));  // open: Reset
  Decodificar_7_seguimentos decodificar_7_seguimentos_1 (
    .A(1'b0), .B(contador0_5_1_a), .C(contador0_5_1_b), .D(contador0_5_1_c),
    .a_2(decodificar_7_seguimentos_1_a_2), .b_2(decodificar_7_seguimentos_1_b_2),
    .c_2(decodificar_7_seguimentos_1_c_2), .d_2(decodificar_7_seguimentos_1_d_2),
    .e(decodificar_7_seguimentos_1_e), .f(decodificar_7_seguimentos_1_f), .g(decodificar_7_seguimentos_1_g));
  nor nor_2 (nor_2_out, contador0_5_1_c, contador0_5_1_b, contador0_5_1_a);
  Decodificar_7_seguimentos decodificar_7_seguimentos_2 (
    .A(contador0_9_1_a), .B(contador0_9_1_b), .C(contador0_9_1_c), .D(contador0_9_1_d),
    .a_2(decodificar_7_seguimentos_2_a_2), .b_2(decodificar_7_seguimentos_2_b_2),
    .c_2(decodificar_7_seguimentos_2_c_2), .d_2(decodificar_7_seguimentos_2_d_2),
    .e(decodificar_7_seguimentos_2_e), .f(decodificar_7_seguimentos_2_f), .g(decodificar_7_seguimentos_2_g));
  Decodificar_7_seguimentos decodificar_7_seguimentos_3 (
    .A(1'b0), .B(1'b0), .C(contador0_2_1_a), .D(contador0_2_1_b), .a_2(decodificar_7_seguimentos_3_a_2),
    .b_2(decodificar_7_seguimentos_3_b_2), .c_2(decodificar_7_seguimentos_3_c_2),
    .d_2(decodificar_7_seguimentos_3_d_2), .e(decodificar_7_seguimentos_3_e),
    .f(decodificar_7_seguimentos_3_f), .g(decodificar_7_seguimentos_3_g));
  nor nor_3 (nor_3_out, contador0_9_2_a, contador0_9_2_b, contador0_9_2_c, contador0_9_2_d);
  nor nor_4 (nor_4_out, contador0_5_2_a, contador0_5_2_a, contador0_5_2_a);
  nor nor_5 (nor_5_out, contador0_9_3_a, contador0_9_3_b, contador0_9_3_c, contador0_9_3_d);
  _7_Segment_Display u_7_segment_display_1 (
    .g(decodificar_7_seguimentos_3_g), .f(decodificar_7_seguimentos_3_f),
    .a(decodificar_7_seguimentos_3_a_2), .b(decodificar_7_seguimentos_3_b_2),
    .e(decodificar_7_seguimentos_3_e), .d(decodificar_7_seguimentos_3_d_2),
    .c(decodificar_7_seguimentos_3_c_2));  // open: dp
  Decodificar_7_seguimentos decodificar_7_seguimentos_4 (
    .A(contador0_9_2_a), .B(contador0_9_2_b), .C(contador0_9_2_c), .D(contador0_9_2_d),
    .a_2(decodificar_7_seguimentos_4_a_2), .b_2(decodificar_7_seguimentos_4_b_2),
    .c_2(decodificar_7_seguimentos_4_c_2), .d_2(decodificar_7_seguimentos_4_d_2),
    .e(decodificar_7_seguimentos_4_e), .f(decodificar_7_seguimentos_4_f), .g(decodificar_7_seguimentos_4_g));
  Decodificar_7_seguimentos decodificar_7_seguimentos_5 (
    .A(1'b0), .B(contador0_5_2_a), .C(contador0_5_2_b), .D(contador0_5_2_c),
    .a_2(decodificar_7_seguimentos_5_a_2), .b_2(decodificar_7_seguimentos_5_b_2),
    .c_2(decodificar_7_seguimentos_5_c_2), .d_2(decodificar_7_seguimentos_5_d_2),
    .e(decodificar_7_seguimentos_5_e), .f(decodificar_7_seguimentos_5_f), .g(decodificar_7_seguimentos_5_g));
  Decodificar_7_seguimentos decodificar_7_seguimentos_6 (
    .A(contador0_9_3_a), .B(contador0_9_3_b), .C(contador0_9_3_c), .D(contador0_9_3_d),
    .a_2(decodificar_7_seguimentos_6_a_2), .b_2(decodificar_7_seguimentos_6_b_2),
    .c_2(decodificar_7_seguimentos_6_c_2), .d_2(decodificar_7_seguimentos_6_d_2),
    .e(decodificar_7_seguimentos_6_e), .f(decodificar_7_seguimentos_6_f), .g(decodificar_7_seguimentos_6_g));
  _7_Segment_Display u_7_segment_display_2 (
    .g(decodificar_7_seguimentos_4_g), .f(decodificar_7_seguimentos_4_f),
    .a(decodificar_7_seguimentos_4_a_2), .b(decodificar_7_seguimentos_4_b_2),
    .e(decodificar_7_seguimentos_4_e), .d(decodificar_7_seguimentos_4_d_2),
    .c(decodificar_7_seguimentos_4_c_2));  // open: dp
  _7_Segment_Display u_7_segment_display_3 (
    .g(decodificar_7_seguimentos_5_g), .f(decodificar_7_seguimentos_5_f),
    .a(decodificar_7_seguimentos_5_a_2), .b(decodificar_7_seguimentos_5_b_2),
    .e(decodificar_7_seguimentos_5_e), .d(decodificar_7_seguimentos_5_d_2),
    .c(decodificar_7_seguimentos_5_c_2));  // open: dp
  _7_Segment_Display u_7_segment_display_4 (
    .g(decodificar_7_seguimentos_6_g), .f(decodificar_7_seguimentos_6_f),
    .a(decodificar_7_seguimentos_6_a_2), .b(decodificar_7_seguimentos_6_b_2),
    .e(decodificar_7_seguimentos_6_e), .d(decodificar_7_seguimentos_6_d_2),
    .c(decodificar_7_seguimentos_6_c_2));  // open: dp
  _7_Segment_Display u_7_segment_display_5 (
    .g(decodificar_7_seguimentos_1_g), .f(decodificar_7_seguimentos_1_f),
    .a(decodificar_7_seguimentos_1_a_2), .b(decodificar_7_seguimentos_1_b_2),
    .e(decodificar_7_seguimentos_1_e), .d(decodificar_7_seguimentos_1_d_2),
    .c(decodificar_7_seguimentos_1_c_2));  // open: dp
  _7_Segment_Display u_7_segment_display_6 (
    .g(decodificar_7_seguimentos_2_g), .f(decodificar_7_seguimentos_2_f),
    .a(decodificar_7_seguimentos_2_a_2), .b(decodificar_7_seguimentos_2_b_2),
    .e(decodificar_7_seguimentos_2_e), .d(decodificar_7_seguimentos_2_d_2),
    .c(decodificar_7_seguimentos_2_c_2));  // open: dp
endmodule

module Contador0_5 (
  input  Reset,
  input  Clock,
  output C,
  output B,
  output A
);

  wire and_1_out, and_2_out, or_1_out;

  J_K_Flip_Flop j_k_ff_1 (.J(1'b1), .clk(Clock), .K(1'b1), .Q(C), .reset(or_1_out));  // open: Qn, preset, en
  and and_1 (and_1_out, B, A);
  J_K_Flip_Flop j_k_ff_2 (.J(C), .clk(Clock), .K(C), .Q(B), .reset(or_1_out));  // open: Qn, preset, en
  and and_2 (and_2_out, C, B);
  J_K_Flip_Flop j_k_ff_3 (.J(and_2_out), .clk(Clock), .K(and_2_out), .Q(A), .reset(or_1_out));  // open: Qn, preset, en
  or or_1 (or_1_out, and_1_out, Reset);
endmodule

module Decodificar_7_seguimentos (
  input  A,
  input  B,
  input  C,
  input  D,
  output a_2,
  output b_2,
  output c_2,
  output d_2,
  output e,
  output f,
  output g
);

  wire and_1_out, and_2_out, and_3_out, and_4_out, and_5_out, and_6_out, and_7_out, and_8_out, and_9_out,
       not_1_out, not_2_out, not_3_out, not_4_out, not_5_out, not_6_out, not_7_out, not_8_out, not_9_out,
       xnor_1_out, xnor_2_out, xor_1_out;

  not not_1 (not_1_out, D);
  not not_2 (not_2_out, C);
  not not_3 (not_3_out, B);
  not not_4 (not_4_out, B);
  not not_5 (not_5_out, D);
  and and_1 (and_1_out, C, not_5_out);
  not not_6 (not_6_out, B);
  and and_2 (and_2_out, C, not_5_out);
  and and_3 (and_3_out, B, not_2_out);
  and and_4 (and_4_out, not_2_out, not_5_out);
  xor xor_1 (xor_1_out, C, B);
  not not_7 (not_7_out, C);
  and and_5 (and_5_out, B, not_7_out, D);
  and and_6 (and_6_out, not_4_out, C);
  not not_8 (not_8_out, D);
  and and_7 (and_7_out, not_6_out, not_8_out);
  and and_8 (and_8_out, B, not_1_out);
  and and_9 (and_9_out, not_4_out, not_5_out);
  xnor xnor_1 (xnor_1_out, B, D);
  or or_1 (a_2, A, C, xnor_1_out);
  not not_9 (not_9_out, C);
  or or_2 (e, and_7_out, and_2_out);
  xnor xnor_2 (xnor_2_out, D, C);
  or or_3 (c_2, B, D, not_9_out);
  or or_4 (d_2, and_9_out, and_5_out, and_6_out, and_1_out, A);
  or or_5 (f, and_8_out, and_3_out, and_4_out, A);
  or or_6 (g, A, and_2_out, xor_1_out);
  or or_7 (b_2, xnor_2_out, not_3_out);
endmodule

module Contador0_2 (
  input  Reset,
  input  Clock,
  output B,
  output A
);

  wire and_1_out, or_1_out;

  J_K_Flip_Flop j_k_ff_1 (.J(1'b1), .clk(Clock), .K(1'b1), .Q(B), .reset(or_1_out));  // open: Qn, preset, en
  J_K_Flip_Flop j_k_ff_2 (.J(B), .clk(Clock), .K(B), .Q(A), .reset(or_1_out));  // open: Qn, preset, en
  and and_1 (and_1_out, B, A);
  or or_1 (or_1_out, and_1_out, Reset);
endmodule
