// Logisim project maquina.circ as structural Verilog: 1 circuit, main circuit main
module main (
  input  A,
  input  B,
  input  C,
  input  D,
  output out_5,
  output out_6,
  output out_7,
  output out_8
);

  wire and_1_out, and_2_out, and_3_out, not_1_out, not_2_out, not_4_out, or_1_out;

  not not_1 (not_1_out, A);
  not not_2 (not_2_out, B);
  or or_1 (or_1_out, not_2_out, not_1_out);
  and and_1 (and_1_out, not_4_out, not_2_out, D);
  and and_2 (and_2_out, D, not_4_out, not_1_out);
  and and_3 (and_3_out, D, not_2_out, not_1_out);
  // NOT_Gate not_3 has open pins: in=D, out=open
  not not_4 (not_4_out, C);
  and and_4 (out_7, C, or_1_out);
  or or_2 (out_8, and_1_out, and_2_out, and_3_out);

  assign out_5 = A;
  assign out_6 = B;
endmodule
